# Fritzing sketch L298_Connections (saved by Fritzing 0.9.4)

parts:
  L298N1 = L298N DC motor driver
  Mod1 = Arduino Sensor Shield v5.0
  M1 = DC Motor
  M2 = DC Motor
  J1 = Piezo Speaker

nets:
  N1: L298N1.OUT1, M2.pin_2
  N2: L298N1.OUT2, M2.pin_1
  N3: L298N1.OUT3, M1.pin_2
  N4: L298N1.OUT4, M1.pin_1
  N5: L298N1.ENA, Mod1.6-S, Mod1.ParallelLCD-D6
  N6: L298N1.ENB, L298N1.IN4, Mod1.5-S, Mod1.4-S, Mod1.ParallelLCD-D4, Mod1.ParallelLCD-D5
  N7: L298N1.IN1, Mod1.12-S, Mod1.ParallelLCD-D12
  N8: L298N1.IN2, Mod1.8-S, Mod1.ParallelLCD-D8
  N9: L298N1.IN3, Mod1.7-S, Mod1.ParallelLCD-D7
  N10: Mod1.AREF-G, Mod1.GND-G, J1.pin1
  N11: Mod1.11-S, Mod1.10-S, Mod1.ParallelLCD-D11, Mod1.ParallelLCD-D10, J1.pin2

custom parts:
  L298N DC motor driver: 2x DC motor driver with 78M05 positive voltage regulator (7..35 V) L298N: max 46 V, 2 A Set 5 V Enable jumper to enable 5 V regultor (needed for the L298N) and +5 V output at screw terminal or supply external +5 V at screw terminal Set ENA and/or ENB to +5 V to enable motor permanently or supply ENA and/or ENB with PWM signal IN1 and IN2 set rotation directory for motor A (OUT1/OUT2) IN2 and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
  Arduino Sensor Shield v5.0: Arduino Sensor Shield v5.0 provides I2C interface, Bluetooth module communication interface, SD card module communication interface, APC220 wireless RF modules communication interface, RB URF V1.1 ultrasonic sensors interface, 12864 LCD serial and parallel interface, 32 servo controller interfaces. In addition (with the sel jumper removed) allows an external power supply for the servos as the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
